// Logisim project alu.circ as structural Verilog: 1 circuit, main circuit alu
module alu (
  input  [31:0] A,
  input  [31:0] B,
  input  [3:0] ALUSel,
  output [31:0] Result
);

  wire [31:0] add0;

  Adder #(.width(32)) adder_1 (.a(A), .b(B), .out(add0));  // open: cin, cout
  // AND_Gate and_1 is placed but not wired
  // OR_Gate or_1 is placed but not wired
  // XOR_Gate xor_1 is placed but not wired
  Shifter shifter_1 ();  // open: in, dist, out
  Shifter shifter_2 ();  // open: in, dist, out
  Shifter shifter_3 ();  // open: in, dist, out
  Comparator #(.width(16)) comparator_1 ();  // open: a, b, gt, eq, lt
  Divider #(.width(16)) divider_1 ();  // open: a, b, out, upper, rem
  Divider #(.width(16)) divider_2 ();  // open: a, b, out, upper, rem
  Multiplier #(.width(1)) multiplier_1 ();  // open: a, b, out, cin, cout
  Multiplier #(.width(1)) multiplier_2 ();  // open: a, b, out, cin, cout
  Subtractor #(.width(16)) subtractor_1 ();  // open: a, b, out, bin, bout
  Multiplexer #(.select(3), .enable("false")) multiplexer_1 ();  // open: in0, in1, in2, in3, in4, in5, in6, in7, out, sel
  Multiplier #(.width(1)) multiplier_3 ();  // open: a, b, out, cin, cout
  Subtractor #(.width(16)) subtractor_2 ();  // open: a, b, out, bin, bout

  // Notes on the sheet:
  //   INPUTS to your circuit
  //   and
  //   or
  //   xor
  //   srl
  //   sra
  //   sll
  //   slt
  //   divu
  //   remu
  //   mul
  //   mulhu
  //   sub
  //   bsel
  //   DON'T CHANGE THE LOCATIONS OF THE INPUTS AND OUTPUTS!
  //   OUTPUT from your circuit
endmodule
